# Fritzing sketch gm70_connection (saved by Fritzing 0.9.3b)
breadboards: 1

parts:
  Part1 = Audio Jack Breakout
  R1 = Resistor [tolerance=±5% resistance=2.2k power=25 package="1206 [SMD]"]
  USBTTL1 = USB TTL Serial Cable

nets:
  GND: Part1.GND, Part1.RING_SHUNT, USBTTL1.GND
  N1: Part1.TIP, R1.Pin_1, USBTTL1.RX
  N2: R1.Pin_0, USBTTL1.5V

notes:
  GM-70
  WHITE: Serial RX
